# Fritzing sketch c (saved by Fritzing 0.9.4)
breadboards: 1

parts:
  Power_plug1 = Power plug
  LED2 = LED - 5mm [color="Red (633nm)" package="5 mm [THT]"]
  R1 = 330 Ω Resistor [package=THT]

nets:
  N1: Power_plug1.GND, R1.Pin_1
  N2: Power_plug1.VCC, LED2.anode
  N3: LED2.cathode, R1.Pin_0

custom parts:
  330 Ω Resistor: A generic resistor (0.25W)
