# Fritzing sketch e (saved by Fritzing 0.9.4)
breadboards: 1

parts:
  Power_plug1 = Power plug
  R2 = Rotary Potentiometer (Large) [maximum_resistance=100kΩ package=THT]
  R3 = 330 Ω Resistor [package=THT]
  LED1 = LED - 5mm [color="Red (633nm)" package="5 mm [THT]"]

nets:
  N1: Power_plug1.GND, R2.leg2, LED1.cathode
  N2: Power_plug1.VCC, R2.leg1
  N3: R2.wiper, R3.Pin_0
  N4: R3.Pin_1, LED1.anode

custom parts:
  330 Ω Resistor: A generic resistor (0.25W)
