# Fritzing sketch f (saved by Fritzing 0.9.4)
breadboards: 1

parts:
  Power_plug1 = Power plug
  74HC1 = DIP - 14 pins [chip_label=74HC04 package="DIP (Dual Inline) [THT]"]

nets:
  N1: Power_plug1.GND, 74HC1.pin7
  N2: Power_plug1.VCC, 74HC1.pin1, 74HC1.pin14

notes:
  Output
  Input

custom parts:
  DIP - 14 pins: A DIP stand-in part for whatever IC you want. With 14 pins on a 300mil dual inline package (DIP) footprint.
