# Fritzing sketch h (saved by Fritzing 0.9.4)
breadboards: 1

parts:
  Power_plug1 = Power plug
  74HC1 = DIP - 14 pins [chip_label=74HC04 package="DIP (Dual Inline) [THT]"]
  R1 = Rotary Potentiometer (Large) [maximum_resistance=100kΩ package=THT]

nets:
  N1: Power_plug1.GND, 74HC1.pin7, R1.leg2
  N2: Power_plug1.VCC, 74HC1.pin14, R1.leg1
  N3: 74HC1.pin1, R1.wiper

notes:
  Output
  Input

custom parts:
  DIP - 14 pins: A DIP stand-in part for whatever IC you want. With 14 pins on a 300mil dual inline package (DIP) footprint.
