# Fritzing sketch a (saved by Fritzing 0.9.4)
breadboards: 1

parts:
  Power_plug1 = Power plug
  74LS1 = 74LS153 [chip_label=74LS153 package="DIP (Dual Inline) [THT]"]
  74LS2 = 74LS32 [chip_label=74LS32 package="DIP (Dual Inline) [THT]"]
  74LS3 = 74LS08 [chip_label=74LS08 package="DIP (Dual Inline) [THT]"]
  74LS4 = 74LS153 [chip_label=74LS153 package="DIP (Dual Inline) [THT]"]
  74LS5 = 74LS74 [chip_label=74LS74 package="DIP (Dual Inline) [THT]"]
  74LS6 = 74LS76 [chip_label=74LS76 package="DIP (Dual Inline) [THT]"]

nets:
  N1: Power_plug1.GND, 74LS1.pin1, 74LS1.pin8, 74LS2.pin7, 74LS3.pin7, 74LS4.pin1, 74LS4.pin8, 74LS5.pin7, 74LS6.pin13, 74LS6.pin16
  N2: Power_plug1.VCC, 74LS1.pin16, 74LS2.pin14, 74LS3.pin14, 74LS4.pin16, 74LS5.pin14, 74LS6.pin5
  N3: 74LS1.pin7, 74LS2.pin1, 74LS3.pin1
  N4: 74LS2.pin2, 74LS3.pin2, 74LS4.pin3, 74LS5.pin5
  N5: 74LS2.pin3, 74LS4.pin6
  N6: 74LS2.pin8, 74LS5.pin3
  N7: 74LS2.pin9, 74LS6.pin1
  N8: 74LS2.pin10, 74LS6.pin15
  N9: 74LS3.pin3, 74LS4.pin4
  N10: 74LS3.pin8, 74LS6.pin4
  N11: 74LS3.pin9, 74LS4.pin14
  N12: 74LS3.pin10, 74LS4.pin2
  N13: 74LS4.pin5, 74LS5.pin6
  N14: 74LS4.pin7, 74LS5.pin2

notes:
  y
  x
  z
  w
  CLOCK
  RESET
  ACC
  y1
  y2
  y4
  y3

custom parts:
  74LS153: 2 * 4-input multiplexer
  74LS32: 4 * 2-input or
  74LS08: 4 * 2-input and
  74LS74: 2 * DFF
  74LS76: 2 * JKFF
