# Fritzing sketch b (saved by Fritzing 0.9.4)
breadboards: 1

parts:
  Power_plug1 = Power plug
  R1 = Trimmer Potentiometer [maximum_resistance=10kΩ package=THT]
  R2 = Resistor [tolerance=±5% resistance=1k package=THT]
  IC1 = IC, DIP package, 14 pins [chip_label="IC 7400"]
  IC2 = IC, DIP package, 14 pins [chip_label="IC 7400"]
  IC3 = IC, DIP package, 14 pins [chip_label="IC 7400"]

nets:
  N1: Power_plug1.GND, R1.leg1, IC1.pin7, IC2.pin7, IC3.pin7
  N2: Power_plug1.VCC, R1.leg2, R2.Pin_0, IC1.pin14, IC2.pin14, IC3.pin14
  N3: R1.wiper, IC1.pin2
  N4: R2.Pin_1, IC1.pin1
  N5: IC1.pin3, IC1.pin4, IC1.pin5
  N6: IC1.pin6, IC1.pin12, IC1.pin13
  N7: IC1.pin8, IC2.pin12, IC2.pin13
  N8: IC1.pin9, IC1.pin10, IC1.pin11
  N9: IC2.pin1, IC2.pin2, IC2.pin8
  N10: IC2.pin3, IC2.pin4, IC2.pin5
  N11: IC2.pin6, IC3.pin1, IC3.pin2
  N12: IC2.pin9, IC2.pin10, IC2.pin11
  N13: IC3.pin3, IC3.pin4, IC3.pin5
  N14: IC3.pin6, IC3.pin12, IC3.pin13
  N15: IC3.pin9, IC3.pin10, IC3.pin11

notes:
  power
