# Fritzing sketch c (saved by Fritzing 0.9.4)
breadboards: 1

parts:
  Power_plug1 = Power plug
  R1 = Trimmer Potentiometer [maximum_resistance=10kΩ package=THT]
  R2 = Resistor [tolerance=±5% resistance=1k package=THT]
  IC1 = IC, DIP package, 14 pins [chip_label="IC 7400"]

nets:
  N1: Power_plug1.GND, R1.leg1, IC1.pin7
  N2: Power_plug1.VCC, R1.leg2, R2.Pin_0, IC1.pin14
  N3: R1.wiper, IC1.pin2
  N4: R2.Pin_1, IC1.pin1
  N5: IC1.pin3, IC1.pin4, IC1.pin5

notes:
  power
