# Fritzing sketch a (saved by Fritzing 0.9.4)
breadboards: 4

parts:
  LED1 = LED - 5mm [color="Red (633nm)" package="5 mm [THT]"]
  LED2 = LED - 5mm [color="Red (633nm)" package="5 mm [THT]"]
  LED3 = LED - 5mm [color="Red (633nm)" package="5 mm [THT]"]
  LED4 = LED - 5mm [color="Red (633nm)" package="5 mm [THT]"]
  LED5 = LED - 5mm [color="Red (633nm)" package="5 mm [THT]"]
  R1 = Resistor [tolerance=±5% resistance=220 package=THT]
  R2 = Resistor [tolerance=±5% resistance=220 package=THT]
  R3 = Resistor [tolerance=±5% resistance=220 package=THT]
  R4 = Resistor [tolerance=±5% resistance=220 package=THT]
  R5 = Resistor [tolerance=±5% resistance=220 package=THT]
  VCC1 = Battery
  IC1 = IC, DIP package, 14 pins [chip_label="IC7493 counter"]
  IC2 = IC, DIP package, 24 pins [chip_label="ic 74154"]
  IC3 = IC, DIP package, 24 pins [chip_label="ic 74154"]
  IC4 = IC, DIP package, 14 pins [chip_label="IC7432 or"]
  IC5 = IC, DIP package, 14 pins [chip_label="IC7432 or"]
  IC6 = IC, DIP package, 14 pins [chip_label="IC7432 or"]
  IC7 = IC, DIP package, 14 pins [chip_label="IC7432 or"]
  IC8 = IC, DIP package, 14 pins [chip_label="IC7432 or"]
  IC10 = IC, DIP package, 14 pins [chip_label="IC7408 and"]
  IC11 = IC, DIP package, 14 pins [chip_label="IC7410 3nand"]
  IC9 = IC, DIP package, 14 pins [chip_label="IC7404 not"]

nets:
  N1: LED1.cathode, R2.Pin_0
  N2: LED1.anode, IC8.pin11
  N3: LED2.cathode, R3.Pin_0
  N4: LED2.anode, IC7.pin6
  N5: LED3.cathode, R4.Pin_0
  N6: LED3.anode, IC7.pin8
  N7: LED4.cathode, R5.Pin_0
  N8: LED4.anode, IC7.pin11
  N9: LED5.cathode, R1.Pin_0
  N10: LED5.anode, IC8.pin8
  N11: R1.Pin_1, R2.Pin_1, R3.Pin_1, R4.Pin_1, R5.Pin_1, IC1.pin10, IC2.pin12, IC3.pin12, IC4.pin7, IC5.pin7, IC6.pin7, IC7.pin7, IC8.pin7, IC10.pin7, IC11.pin7, IC9.pin7
  N12: VCC1.+, IC3.pin24, IC4.pin14, IC5.pin14, IC6.pin14, IC7.pin14, IC8.pin14, IC10.pin14, IC11.pin14, IC9.pin14
  N13: IC1.pin1, IC1.pin12, IC2.pin23, IC3.pin23
  N14: IC1.pin2, IC1.pin3, IC8.pin6
  N15: IC1.pin5, IC2.pin24
  N16: IC1.pin8, IC2.pin21, IC3.pin21
  N17: IC1.pin9, IC2.pin22, IC3.pin22
  N18: IC1.pin11, IC2.pin20, IC3.pin20
  N19: IC2.pin1, IC4.pin1
  N20: IC2.pin2, IC4.pin2
  N21: IC2.pin3, IC4.pin13
  N22: IC2.pin4, IC4.pin12
  N23: IC2.pin5, IC4.pin9
  N24: IC2.pin6, IC5.pin1
  N25: IC2.pin7, IC5.pin2
  N26: IC2.pin8, IC5.pin4
  N27: IC2.pin9, IC5.pin5
  N28: IC2.pin10, IC8.pin2
  N29: IC2.pin19, IC9.pin12
  N30: IC3.pin1, IC5.pin13
  N31: IC3.pin2, IC5.pin12
  N32: IC3.pin3, IC7.pin1
  N33: IC3.pin4, IC7.pin2
  N34: IC3.pin5, IC7.pin5
  N35: IC3.pin6, IC6.pin1
  N36: IC3.pin7, IC6.pin2
  N37: IC3.pin8, IC6.pin5
  N38: IC3.pin9, IC6.pin13
  N39: IC3.pin10, IC6.pin12
  N40: IC3.pin11, IC6.pin10
  N41: IC3.pin13, IC6.pin9
  N42: IC3.pin14, IC8.pin5
  N43: IC3.pin19, IC9.pin10
  N44: IC4.pin3, IC7.pin13
  N45: IC4.pin8, IC7.pin10
  N46: IC4.pin10, IC4.pin11
  N47: IC5.pin3, IC8.pin13
  N48: IC5.pin6, IC8.pin10
  N49: IC5.pin11, IC7.pin12
  N50: IC6.pin3, IC6.pin4
  N51: IC6.pin6, IC7.pin9
  N52: IC6.pin8, IC8.pin9
  N53: IC6.pin11, IC8.pin12
  N54: IC7.pin3, IC7.pin4
  N55: IC8.pin1, IC11.pin6, IC9.pin3, IC9.pin5
  N56: IC8.pin3, IC8.pin4
  N57: IC10.pin1, IC10.pin4, IC9.pin4
  N58: IC10.pin2, IC9.pin2
  N59: IC10.pin3, IC9.pin13
  N60: IC10.pin6, IC9.pin11
