# Fritzing sketch a (saved by Fritzing 0.9.4)
breadboards: 6

parts:
  R1 = Resistor [tolerance=±5% resistance=220 package=THT]
  R2 = Resistor [tolerance=±5% resistance=220 package=THT]
  R3 = Resistor [tolerance=±5% resistance=220 package=THT]
  R4 = Resistor [tolerance=±5% resistance=220 package=THT]
  R5 = Resistor [tolerance=±5% resistance=220 package=THT]
  R6 = Resistor [tolerance=±5% resistance=220 package=THT]
  R7 = Resistor [tolerance=±5% resistance=220 package=THT]
  IC1 = IC, DIP package, 16 pins [chip_label="IC 74157"]
  IC2 = IC, DIP package, 16 pins [chip_label="IC 74157"]
  IC3 = IC, DIP package, 16 pins [chip_label="IC 74175"]
  IC4 = IC, DIP package, 16 pins [chip_label="IC 74175"]
  IC5 = IC, DIP package, 24 pins [chip_label="IC 74181"]
  R8 = Resistor [tolerance=±5% resistance=220 package=THT]
  IC10 = IC, DIP package, 14 pins [chip_label="IC 7432"]
  IC9 = IC, DIP package, 14 pins [chip_label="IC 7432"]
  IC7 = IC, DIP package, 14 pins [chip_label="IC 7408"]
  IC6 = IC, DIP package, 14 pins [chip_label="IC 7404"]
  IC8 = IC, DIP package, 14 pins [chip_label="IC 74135"]

nets:
  N1: R1.Pin_0, R2.Pin_0, R3.Pin_0, R4.Pin_0, R5.Pin_0, R6.Pin_0, R7.Pin_0, R8.Pin_0
  N2: R1.Pin_1, R2.Pin_1, R3.Pin_1, R4.Pin_1, R5.Pin_1, R6.Pin_1, R7.Pin_1, IC1.pin2, IC1.pin5, IC1.pin11, IC1.pin14, IC2.pin2, IC2.pin5, IC2.pin11, IC2.pin14, IC3.pin1, IC4.pin1, R8.Pin_1, IC10.pin1, IC10.pin2, IC10.pin5, IC10.pin9, IC10.pin12, IC9.pin1, IC7.pin1, IC7.pin2, IC7.pin5, IC6.pin11, IC6.pin13, IC8.pin1, IC8.pin2, IC8.pin4, IC8.pin5
  N3: IC1.pin1, IC10.pin6
  N4: IC1.pin3, IC5.pin9
  N5: IC1.pin4, IC3.pin4
  N6: IC1.pin6, IC5.pin10
  N7: IC1.pin7, IC3.pin5
  N8: IC1.pin8, IC1.pin15, IC2.pin8, IC2.pin15
  N9: IC1.pin9, IC3.pin12
  N10: IC1.pin10, IC5.pin11
  N11: IC1.pin12, IC3.pin13
  N12: IC1.pin13, IC5.pin13
  N13: IC1.pin16, IC2.pin16
  N14: IC2.pin1, IC10.pin8
  N15: IC2.pin3, IC4.pin2, IC5.pin1
  N16: IC2.pin4, IC4.pin4
  N17: IC2.pin6, IC4.pin7, IC5.pin22
  N18: IC2.pin7, IC4.pin5
  N19: IC2.pin9, IC4.pin12
  N20: IC2.pin10, IC4.pin10, IC5.pin20
  N21: IC2.pin12, IC4.pin13
  N22: IC2.pin13, IC4.pin15, IC5.pin18
  N23: IC3.pin2, IC5.pin2
  N24: IC3.pin7, IC5.pin23
  N25: IC3.pin8, IC4.pin8
  N26: IC3.pin9, IC4.pin9
  N27: IC3.pin10, IC5.pin21
  N28: IC3.pin15, IC5.pin19
  N29: IC3.pin16, IC4.pin16
  N30: IC5.pin3, IC9.pin3
  N31: IC5.pin4, IC7.pin11
  N32: IC5.pin5, IC9.pin11
  N33: IC5.pin6, IC9.pin6
  N34: IC5.pin8, IC6.pin4
  N35: IC10.pin3, IC10.pin4
  N36: IC10.pin7, IC9.pin7
  N37: IC10.pin10, IC10.pin11
  N38: IC10.pin13, IC9.pin5, IC9.pin12, IC6.pin10
  N39: IC10.pin14, IC9.pin14
  N40: IC9.pin2, IC9.pin13, IC7.pin12, IC6.pin12
  N41: IC9.pin4, IC6.pin6
  N42: IC7.pin3, IC7.pin4
  N43: IC7.pin6, IC6.pin3
  N44: IC7.pin7, IC6.pin7, IC8.pin7
  N45: IC7.pin13, IC8.pin6
  N46: IC7.pin14, IC6.pin14, IC8.pin14
  N47: IC6.pin5, IC8.pin3

notes:
  D0
  D2
  D1
  D3
  S2
  S1
  S0
  Clock
